# Fritzing sketch extruder (saved by Fritzing 0.9.3b)

parts:
  Part3 = Arduino Mega 2560 (Rev3)
  LED1 = LED - 3mm [color="Red (633nm)" package="3 mm [THT]"]
  LED2 = LED - 3mm [color="Green (555nm)" package="3 mm [THT]"]
  F1 = Fan - Ventilador [package=THT]
  F2 = Fan - Ventilador [package=THT]
  F3 = Fan - Ventilador [package=THT]
  OMRON1 = OMRON PCB Power Relay – G5LE [part_number="G5LE-1\n" package=THT]
  M1 = Stepper Motor - Bipolar
  M2 = Stepper Motor - Bipolar
  S1 = H-Bridge with L298N
  S2 = H-Bridge with L298N
  U1 = SWITCH-SPST-2 [package=switch-spst-vertical]
  U2 = SWITCH-SPST-2 [package=switch-spst-vertical]
  U3 = SWITCH-SPST-2 [package=switch-spst-vertical]
  S4 = Pushbutton [package="[SMD]"]
  S5 = SWITCH-SPST-2 [package=r_sw_th]
  U4 = SWITCH-SPST-2 [package=switch-spst-vertical]
  R1 = Resistor [tolerance=±5% resistance=0 package="0805 [SMD]"]
  OMRON2 = OMRON PCB Power Relay – G5LE [part_number="G5LE-1\n" package=THT]
  JACK1 = 2.1mm Barrel Jack with Terminal Block
  JACK2 = 2.1mm Barrel Jack with Terminal Block

nets:
  GND: Part3.GND, Part3.D13_PWM, LED1.cathode, LED2.cathode, OMRON1.COIL1, S1.GND, S2.GND, U1.P, U2.P, U3.P, S4.Pin_3, S4.Pin_4, U4.P, OMRON2.COIL1
  N1: Part3.D12_PWM, LED2.anode
  N2: Part3.D11_PWM, LED1.anode
  N3: Part3.D10_PWM, OMRON1.COIL2
  N4: Part3.D9_PWM, S2.IN4
  N5: Part3.D8_PWM, S2.IN3
  5V: Part3.5V, S1.5V, S2.5V
  N6: Part3.D2_PWM, S1.IN1
  N7: Part3.D3_PWM, S1.IN2
  N8: Part3.D4_PWM, S1.IN3
  N9: Part3.D5_PWM, S1.IN4
  N10: Part3.D6_PWM, S2.IN1
  N11: Part3.D7_PWM, S2.IN2
  N12: Part3.D22, U3.O
  N13: Part3.D23, U1.O
  N14: Part3.D24, U2.O
  N15: Part3.D25, U4.O
  N16: Part3.D26, OMRON2.COIL2
  5V_2: F1.5V, F2.5V, F3.5V, S1.12V, S2.12V, S5.P
  N17: F1.GND, OMRON1.B, JACK2.POS
  GND_2: F2.GND, F3.GND, OMRON1.C
  N18: M1.A, S1.OUT1-Motor1
  N19: M1.C, S1.OUT2-Motor1
  N20: M1.B, S1.OUT3-Motor2
  N21: M1.D, S1.OUT4-Motor2
  N22: M2.A, S2.OUT1-Motor1
  N23: M2.C, S2.OUT2-Motor1
  N24: M2.B, S2.OUT3-Motor2
  N25: M2.D, S2.OUT4-Motor2
  N26: S5.O, JACK2.NEG
  N27: R1.Pin_0, OMRON2.B
  N28: R1.Pin_1, JACK1.POS
  N29: OMRON2.C, JACK1.NEG

notes:
  Indicadors temperatura fred/calent
  Refrigeració filament
  Refrigeració continua placa base
  Placa base Arduino Mega 2650
  Motor de passos: extrusor
  Motor de passos: bobina
  Int: General
  Int:Refrigeració filament
  Int: Extrusió
  Int: Invertir direcció
  PBtn: Emergency STOP
  Int: Habilitar recullidor
  habilitar recullidor = NO --> no holding
  Controladores motors
  L298n
  Font d'alimentació 12V DC
  Relé circuit refrigeració

custom parts:
  Fan - Ventilador: Ventilador de 2 pines, se encuentra comunmente en computadoras de escritorio
  H-Bridge with L298N: h-bridge

// code stored in the sketch: .ino
/*

  Extrusora de PLA controlada per Arduino Mega 2560.

  Projecte: 
  - https://github.com/bertugarangou/ExtrusoraPLA

  Circuit:
  - Extrusora feta per Albert Garangou,
    com a Treball de Recerca a 2n de Batxillerat,
    curs 2018/2019, tutor Jordi Fanals Oriol,
    codi amb Arduino IDE 1.8.5,

    Copyright (c) 2018 Albert Garangou Culebras (albertgarangou@gmail.com)
    This Font Software is licensed under the SIL Open Font License, Version 1.1.

*/
